# Fritzing sketch Monkey (saved by Fritzing 0.9.3b)

parts:
  M1 = DC Motor
  VCC1 = Battery
  U1 = Module 4 Relais 5V [package="Module 4 Relais 5V"]
  SparkFun_ESP32_Thing1 = SparkFun ESP32 Thing [part_number=DEV-13907]

nets:
  N1: M1.pin_1, U1.K3-NF
  N2: M1.pin_2, U1.K4-NF
  N3: VCC1.+, U1.K2-NF
  VCC: U1.VCC, SparkFun_ESP32_Thing1.3.3V
  GND: U1.GND, SparkFun_ESP32_Thing1.GND
  N4: U1.IN2, SparkFun_ESP32_Thing1.12
  N5: U1.IN3, SparkFun_ESP32_Thing1.14
  N6: U1.IN4, SparkFun_ESP32_Thing1.27
  N7: U1.K3-Com, U1.K2-NO, U1.K4-NO
  N8: U1.K4-Com, U1.K3-NO
  N9: U1.JD-VCC, SparkFun_ESP32_Thing1.VUSB-RAW

notes:
  JBTek 4 relay module
  Using three relays allows the controller to run the motor forwards or backwards

custom parts:
  Module 4 Relais 5V: Module 4 Relais 5V 4x SPD-06VDC-SD-C
  SparkFun ESP32 Thing: The SparkFun ESP32 Thing is a comprehensive development platform for Espressif’s ESP32, their super-charged version of the popular ESP8266. Like the 8266, the ESP32 is a WiFi-compatible microcontroller, but to that it adds support for Bluetooth low-energy (i.e BLE, BT4.0, Bluetooth Smart), and nearly 30 I/O pins. The ESP32’s power and versatility will make it the foundation of IoT and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
